# Fritzing sketch ShemaSpajanja (saved by Fritzing 0.9.3b)
breadboards: 1

parts:
  FRDM1 = Freescale FRDM KL25Z
  Part1 = ETF Joystick
  Banggood_Display1 = Banggood Display

nets:
  3.3V: FRDM1.3.3V, Banggood_Display1.VCC, Banggood_Display1.LED
  N1: FRDM1.PTA20, Banggood_Display1.RST
  5V: FRDM1.5V, Part1.+5V
  N2: FRDM1.GND#5, Banggood_Display1.GND
  N3: FRDM1.GND#6, Part1.GND
  N4: FRDM1.PTB1, Part1.VRx
  N5: FRDM1.PTB2, Part1.VRy
  N6: FRDM1.PTE5, Part1.SW
  N7: FRDM1.PTA17, Banggood_Display1.SCK
  N8: FRDM1.PTA16, Banggood_Display1.SDI
  N9: FRDM1.PTC17, Banggood_Display1.SDO
  N10: FRDM1.PTC16, Banggood_Display1.CS
  N11: FRDM1.PTC13, Banggood_Display1.DC

custom parts:
  Freescale FRDM KL25Z: Freescale FRDM razvojni sistem
